# Fritzing sketch 4digit_7seg_driver_LTC-4727JR (saved by Fritzing 0.9.10b)
breadboards: 1

parts:
  U2 = 74HC595 [package="DIP16 [THT]"]
  Pico_H1 = Raspberry Pi Pico H
  U1 = 7-SEGMENT-4DIGIT [part_number=LTC-4727JR package=7-segment-4digit]
  Q1 = NPN-Transistor [part_number=2N3904 package="TO92 [THT]"]
  Q2 = NPN-Transistor [part_number=2N3904 package="TO92 [THT]"]
  Q3 = NPN-Transistor [part_number=2N3904 package="TO92 [THT]"]
  Q4 = NPN-Transistor [part_number=2N3904 package="TO92 [THT]"]
  Vin = DC Power [voltage=9V]
  U3 = Voltage Regulator - 5V [part_number=7805 package="TO220 [THT]"]
  R1 = Resistor [tolerance=±5% power=0.25 resistance=1k package=THT]
  R2 = Resistor [tolerance=±5% power=0.25 resistance=1k package=THT]
  R3 = Resistor [tolerance=±5% power=0.25 resistance=1k package=THT]
  R4 = Resistor [tolerance=±5% power=0.25 resistance=1k package=THT]
  R5 = Resistor [tolerance=±5% power=0.25 resistance=680 package=THT]
  R6 = Resistor [tolerance=±5% power=0.25 resistance=680 package=THT]
  R7 = Resistor [tolerance=±5% power=0.25 resistance=680 package=THT]
  R8 = Resistor [tolerance=±5% power=0.25 resistance=680 package=THT]
  R9 = Resistor [tolerance=±5% power=0.25 resistance=680 package=THT]
  R10 = Resistor [tolerance=±5% power=0.25 resistance=680 package=THT]
  R11 = Resistor [tolerance=±5% power=0.25 resistance=680 package=THT]
  R12 = Resistor [tolerance=±5% power=0.25 resistance=680 package=THT]

nets:
  N1: U2.Q1, R12.Pin_0
  N2: U2.Q2, R9.Pin_0
  N3: U2.Q3, R5.Pin_0
  N4: U2.Q4, R6.Pin_0
  N5: U2.Q5, R8.Pin_0
  N6: U2.Q6, R11.Pin_0
  N7: U2.Q7, R7.Pin_0
  GND: U2.GND, U2.OE, Pico_H1.GND, Q1.E, Q2.E, Q3.E, Q4.E, Vin.V-, U3.GND
  3.3V: U2.MR, U2.VCC
  N8: U2.SH_CP, U2.ST_CP, Pico_H1.GP2
  N9: U2.DS, Pico_H1.GP1
  N10: U2.Q0, R10.Pin_0
  N11: Pico_H1.VSYS, U3.output_voltage
  3.3V Output: Pico_H1.3V3
  N12: Pico_H1.GP13, R1.Pin_1
  N13: Pico_H1.GP12, R2.Pin_1
  N14: Pico_H1.GP11, R3.Pin_1
  N15: Pico_H1.GP10, R4.Pin_1
  N16: U1.1, Q4.C
  N17: U1.2, Q3.C
  N18: U1.3, R5.Pin_1
  N/C: U1.4, U1.9
  N19: U1.5, R6.Pin_1
  N20: U1.6, Q2.C
  N21: U1.7, R7.Pin_1
  N22: U1.8, Q1.C
  N23: U1.11, R8.Pin_1
  N24: U1.13, R9.Pin_1
  N25: U1.14, R10.Pin_1
  N26: U1.15, R11.Pin_1
  N27: U1.16, R12.Pin_1
  N28: Q1.B, R1.Pin_0
  N29: Q2.B, R2.Pin_0
  N30: Q3.B, R3.Pin_0
  N31: Q4.B, R4.Pin_0
  N32: Vin.V+, U3.input_voltage

notes:
  R5-R12 >= 560Ω each
  Common Cathode
  16
  15
  11
  5
  7
  3
  13
  14

custom parts:
  Raspberry Pi Pico H: Raspberry Pi Pico H. Based around the RP2040 microcontroller the Pico H is a low cost microcontroller device bringing Raspberry Pi quality, cost, and easy of use to the microcontroller space.
